# Fritzing sketch schema1 (saved by Fritzing 0.9.0b)
breadboards: 1

parts:
  Part1 = Arduino Yun
  LED1 = LED - 5mm [color="Red (633nm)" package="5 mm [THT]"]
  LED2 = LED - 5mm [color="Yellow (585nm)" package="5 mm [THT]"]
  LED3 = LED - 5mm [color="Green (565nm)" package="5 mm [THT]"]
  R1 = Resistor [tolerance=±5% resistance=220 package=THT]
  R2 = Resistor [tolerance=±5% resistance=220 package=THT]
  R3 = Resistor [tolerance=±5% resistance=220 package=THT]
  R4 = Temperature Sensor (Thermistor) [thermistor_type=NTC package=THT]
  R5 = Temperature Sensor (Thermistor) [thermistor_type=NTC package=THT]
  R6 = Resistor [tolerance=±5% resistance=10k package=THT]
  R7 = Resistor [tolerance=±5% resistance=10k package=THT]
  RHT1 = Humidity and Temperature Sensor RHT03
  R8 = Resistor [tolerance=±5% resistance=10k package=THT]

nets:
  N1: Part1.A0, R5.pin_0, R7.Pin_1
  N2: Part1.A5/SCL, R4.pin_0, R6.Pin_1
  N3: Part1.5V, R4.pin_1, R5.pin_1, RHT1.GND_1, R8.Pin_1
  N4: Part1.D11_PWM/MOSI, RHT1.Vcc, R8.Pin_0
  N5: Part1.D2, R3.Pin_0
  N6: Part1.D3_PWM, R2.Pin_0
  N7: Part1.D4, R1.Pin_0
  N8: Part1.GND, LED1.cathode, LED2.cathode, LED3.cathode, R6.Pin_0, R7.Pin_0, RHT1.GND_2
  N9: LED1.anode, R1.Pin_1
  N10: LED2.anode, R2.Pin_1
  N11: LED3.anode, R3.Pin_1

notes:
  DHT 11
  LONG WIRE
  S, , +, -
